# Fritzing sketch Wiring (saved by Fritzing 1.0.2b)
breadboards: 1

parts:
  Pico_H1 = Raspberry Pi Pico H
  PIR_HC-SR502 = HC-SR501 Body Sensor Module
  DHT1 = DHT11 Humitidy and Temperature Sensor (3 pins)
  Mod1 = KY-004 Key Switch Module [package="Breakout board"]
  Part2 = KY-018 Photoresistor Module [package="Breakout board"]

nets:
  N1: Pico_H1.VBUS, PIR_HC-SR502.VCC
  GND: Pico_H1.GND, PIR_HC-SR502.GND, DHT1.Gnd, Mod1.-, Part2.-
  VIN: Pico_H1.3V3, DHT1.Signal, Mod1.Vin, Part2.Vin
  N2: Pico_H1.GP28_A2, Part2.S
  N3: Pico_H1.GP27_A1, DHT1.Plus
  N4: Pico_H1.GP21, PIR_HC-SR502.OUT
  N5: Pico_H1.GP16, Mod1.S

custom parts:
  Raspberry Pi Pico H: Raspberry Pi Pico H. Based around the RP2040 microcontroller the Pico H is a low cost microcontroller device bringing Raspberry Pi quality, cost, and easy of use to the microcontroller space.
  HC-SR501 Body Sensor Module: Pyroelectric Infrared PIR Motion Sensor Detector Module
  DHT11 Humitidy and Temperature Sensor (3 pins): DHT11 Humidity and Temperature Sensor (3 pins).
  KY-004 Key Switch Module: Arduino Key Switch Module Keyes KY-004 is a push button that will output a high signal when pressed.
  KY-018 Photoresistor Module: KY-018 Photoresistor module, used to measure light intensity. It can determine the presence or absence of light.
